# Fritzing sketch visual_schematic (saved by Fritzing 0.9.3b)
breadboards: 1

parts:
  R1 = Resistor [tolerance=±5% resistance=10k package=THT]
  Componente1 = Arduino Leonardo (Rev3b)
  R2 = Photocell (LDR) [package=THT]
  hc-sr1 = hc-sr04
  LED1 = smd LED [color="Red (633nm)" package="0805 [SMD]"]
  IC1 = ULN2003A [package="SO16 [SMD]"]
  M1 = Stepper Motor - Unipolar

nets:
  N1: R1.Pin_0, Componente1.A0, R2.pin_1
  N2: Componente1.D6_PWM/A7, hc-sr1.Echo
  N3: Componente1.D7, hc-sr1.Trig
  5V: Componente1.5V, R2.pin_0, hc-sr1.VCC, LED1.cathode
  GND: Componente1.GND, hc-sr1.GND, LED1.anode
  N4: Componente1.D9_PWM/A9, IC1.In_4
  N5: Componente1.D10_PWM/A10, IC1.In_3
  N6: Componente1.D11_PWM, IC1.In_2
  N7: Componente1.D12/A11, IC1.In_1
  N8: IC1.Out_6, M1.D
  N9: IC1.Out_5, M1.COMMON_2
  N10: IC1.Out_4, M1.B
  N11: IC1.Out_3, M1.C
  N12: IC1.Out_2, M1.COMMON_1
  N13: IC1.Out_1, M1.A
